// Logisim project brainfuck_cpu.circ as structural Verilog: 1 circuit, main circuit main
module main (
);

  wire and_1_out, and_2_out, and_4_out, and_5_out, BALANCED, C_INST7, C_INST8, CLK, CLK_NO_HALT,
       comparator_2_eq, comparator_5_eq, counter_1_carry, counter_1_q, d_ff_1_q, DEC_BYTE, DEC_DP,
       decoder_1_out0, decoder_1_out1, HALT, HALT_0, HALT_INCDEC, HALT_INPUT, INC_BYTE, INC_DP, INPUT, J_B,
       J_F, keyboard_1_avail, not_1_out, not_2_out, not_3_out, not_4_out, not_5_out, or_1_out, or_2_out,
       or_4_out, or_6_out, or_7_out, or_8_out, OUTPUT, PC_HALT, register_3_q, RST, s_r_ff_1_q, s_r_ff_2_q,
       s_r_ff_3_q, s_r_ff_4_q, s_r_ff_5_q, s_r_ff_7_q;
  wire [3:0] C_INST;
  wire [6:0] keyboard_1_data;
  wire [7:0] adder_3_out, adder_4_out, bit_extender_1_out, counter_2_q, DATA, multiplexer_2_out,
       multiplexer_3_out, multiplexer_4_out, multiplexer_5_out, subtractor_1_out;
  wire [15:0] adder_1_out, adder_2_out, controlled_buffer_1_out, multiplexer_1_out, PC_D, register_1_q,
       register_2_q;

  not not_1 (not_1_out, HALT);
  assign controlled_buffer_1_out = not_1_out ? adder_1_out : 16'bz;  // Controlled_Buffer controlled_buffer_1
  Register #(.width(16)) register_1 (
    .D(controlled_buffer_1_out), .Q(register_1_q), .clk(CLK_NO_HALT));  // open: en, clr
  Register #(.width(16)) register_2 (.D(adder_2_out), .Q(register_2_q), .clk(CLK));  // open: en, clr
  or or_1 (or_1_out, INC_DP, DEC_DP);
  S_R_Flip_Flop s_r_ff_1 (
    .S(INC_BYTE), .clk(CLK_NO_HALT), .R(counter_1_carry), .Q(s_r_ff_1_q));  // open: Qn, preset, reset, en
  S_R_Flip_Flop s_r_ff_2 (
    .S(DEC_BYTE), .clk(CLK_NO_HALT), .R(counter_1_carry), .Q(s_r_ff_2_q));  // open: Qn, preset, reset, en
  or or_2 (or_2_out, C_INST7, C_INST8);
  Adder #(.width(16)) adder_1 (.a(register_1_q), .b(PC_D), .out(adder_1_out));  // open: cin, cout
  Adder #(.width(16)) adder_2 (.a(register_2_q), .b(multiplexer_1_out), .out(adder_2_out));  // open: cin, cout
  Multiplexer #(.width(16), .disabled(0)) multiplexer_1 (
    .in0(16'h1), .in1({16{1'b1}}), .out(multiplexer_1_out), .sel(DEC_DP), .en(or_1_out));
  or or_3 (HALT_INCDEC, s_r_ff_1_q, s_r_ff_2_q);
  Counter #(.width(1), .max('h1)) counter_1 (
    .Q(counter_1_q), .carry(counter_1_carry), .clk(CLK_NO_HALT), .clr(not_2_out));  // open: load, D, count
  not not_2 (not_2_out, HALT_INCDEC);
  Counter counter_2 (
    .load(C_INST8), .count(or_2_out), .Q(counter_2_q), .clk(CLK_NO_HALT), .clr(not_3_out));  // open: D, carry
  not not_3 (not_3_out, or_6_out);
  Decoder decoder_1 (.out0(decoder_1_out0), .out1(decoder_1_out1), .sel(counter_1_q), .en(HALT_INCDEC));
  Adder adder_3 (.a(counter_2_q), .b({8{1'b0}}), .out(adder_3_out), .cin(C_INST7));  // open: cout
  ROM #(.addrWidth(16), .dataWidth(4)) rom_1 (.addr(adder_1_out), .data(C_INST));  // open: sel
  RAM #(.addrWidth(16), .bus("separate")) ram_1 (
    .addr(adder_2_out), .din(multiplexer_5_out), .data(DATA), .str(or_4_out), .clk(CLK_NO_HALT), .ld(1'b1),
    .clr(RST));  // open: sel
  // Probe on multiplexer_5_out
  or or_4 (or_4_out, d_ff_1_q, s_r_ff_3_q);
  Multiplexer #(.width(8), .enable("false")) multiplexer_2 (
    .in0(8'h1), .in1({8{1'b1}}), .out(multiplexer_2_out), .sel(s_r_ff_2_q));
  S_R_Flip_Flop s_r_ff_3 (
    .S(decoder_1_out0), .clk(CLK_NO_HALT), .R(decoder_1_out1), .Q(s_r_ff_3_q));  // open: Qn, preset, reset, en
  Subtractor subtractor_1 (.a(adder_3_out), .b({8{1'b0}}), .out(subtractor_1_out), .bin(C_INST8));  // open: bout
  Comparator comparator_1 (.a(subtractor_1_out), .b(multiplexer_3_out), .eq(BALANCED));  // open: gt, lt
  Multiplexer #(.width(8), .enable("false")) multiplexer_3 (
    .in0({8{1'b1}}), .in1(8'h1), .out(multiplexer_3_out), .sel(s_r_ff_4_q));
  Decoder #(.select(4), .disabled(0)) decoder_2 (
    .out0(HALT_0), .out1(INC_DP), .out2(DEC_DP), .out3(INC_BYTE), .out4(DEC_BYTE), .out5(OUTPUT),
    .out6(INPUT), .out7(J_F), .out8(J_B), .sel(C_INST), .en(PC_HALT));  // open: out9, out10, out11, out12, out13, out14, out15
  Multiplexer #(.width(8), .enable("false")) multiplexer_4 (
    .in0(DATA), .in1(adder_4_out), .out(multiplexer_4_out), .sel(s_r_ff_3_q));
  not not_4 (not_4_out, comparator_2_eq);
  Comparator comparator_2 (.a({8{1'b0}}), .b(DATA), .eq(comparator_2_eq));  // open: gt, lt
  TTY tty_1 (.data(DATA[6:0]), .clk(CLK), .we(OUTPUT));  // open: clr
  Keyboard keyboard_1 (.clk(CLK), .re(1'b1), .avail(keyboard_1_avail), .data(keyboard_1_data));  // open: clr
  Adder adder_4 (.a(DATA), .b(multiplexer_2_out), .out(adder_4_out));  // open: cin, cout
  and and_1 (and_1_out, J_B, not_4_out);
  S_R_Flip_Flop s_r_ff_4 (
    .S(and_1_out), .clk(CLK_NO_HALT), .R(and_2_out), .Q(s_r_ff_4_q));  // open: Qn, preset, reset, en
  and and_2 (and_2_out, C_INST7, BALANCED);
  Multiplexer #(.width(8), .enable("false")) multiplexer_5 (
    .in0(multiplexer_4_out), .in1(bit_extender_1_out), .out(multiplexer_5_out), .sel(d_ff_1_q));
  Clock clock_1 (.out(CLK_NO_HALT));
  Register #(.width(1)) register_3 (.D(not_5_out), .Q(register_3_q), .clk(CLK_NO_HALT));  // open: en, clr
  not not_5 (not_5_out, HALT);
  or or_5 (HALT, HALT_INCDEC, HALT_INPUT, HALT_0);
  Multiplexer #(.width(16), .enable("false")) multiplexer_6 (
    .in0(16'h1), .in1({16{1'b1}}), .out(PC_D), .sel(s_r_ff_4_q));
  and and_3 (CLK, register_3_q, CLK_NO_HALT);
  S_R_Flip_Flop s_r_ff_5 (.Q(s_r_ff_5_q), .preset(HALT_0));  // open: S, clk, R, Qn, reset, en
  or or_6 (or_6_out, s_r_ff_4_q, s_r_ff_7_q);
  S_R_Flip_Flop s_r_ff_6 (
    .S(INPUT), .clk(CLK_NO_HALT), .R(keyboard_1_avail), .Q(HALT_INPUT));  // open: Qn, preset, reset, en
  assign bit_extender_1_out = {{1{1'b0}}, keyboard_1_data};  // Bit_Extender bit_extender_1
  and and_4 (and_4_out, J_F, comparator_5_eq);
  or or_7 (or_7_out, register_3_q, s_r_ff_5_q);
  Multiplexer #(.enable("false")) multiplexer_7 (.in0(or_7_out), .in1(1'b0), .out(PC_HALT), .sel(or_8_out));
  or or_8 (or_8_out, s_r_ff_4_q, s_r_ff_7_q);
  Comparator #(.width(4)) comparator_3 (.a(C_INST), .b(4'b0111), .eq(C_INST7));  // open: gt, lt
  Comparator #(.width(4)) comparator_4 (.a(C_INST), .b(4'b1000), .eq(C_INST8));  // open: gt, lt
  LED led_1 (.in(HALT_INPUT));
  D_Flip_Flop d_ff_1 (.clk(CLK_NO_HALT), .D(HALT_INPUT), .Q(d_ff_1_q));  // open: Qn, preset, en, reset
  Comparator comparator_5 (.a(DATA), .b({8{1'b0}}), .eq(comparator_5_eq));  // open: gt, lt
  S_R_Flip_Flop s_r_ff_7 (
    .S(and_4_out), .clk(CLK_NO_HALT), .R(and_5_out), .Q(s_r_ff_7_q));  // open: Qn, preset, reset, en
  and and_5 (and_5_out, C_INST8, BALANCED);

  // Notes on the sheet:
  //   Brainf**k CPU (mdl. f1)
  //   ROM
  //   RAM
  //   contents of rom_1 (hex, n*v repeats v):
  //   f f 1 f 3 f 3 f 3 f 3 f 3 f 3 f 3 f 3 f 3 f 3 f 1 f 3 f 1 f 3 f 7 f 7 f 3 f 3 f 3 f 3 f 3 f 7 f 1 f
  //   3 f 3 f 3 f 3 f 3 f 3 f 3 f 3 f 2 f 4 f 8 f 1 f 5 f 2 f 3 f 3 f 3 f 3 f 3 f 3 f 7 f 1 f 4 f 4 f 4 f
  //   4 f 4 f 4 f 4 f 4 f 2 f 4 f 8 f 3 f 2 f 2 f 2 f 8 f 1 f 5 f 1 f 1 f 7 f 7 f 4 f 8 f 2 f 7 f 1 f 3 f
  //   2 f 4 f 8 f 1 f 1 f 7 f 2 f 2 f 3 f 1 f 3 f 1 f 4 f 8 f 2 f 7 f 1 f 3 f 2 f 4 f 7 f 1 f 3 f 2 f 4 f
  //   7 f 1 f 3 f 2 f 4 f 7 f 1 f 3 f 2 f 4 f 7 f 1 f 3 f 2 f 4 f 7 f 1 f 3 f 2 f 4 f 7 f 1 f 3 f 2 f 4 f
  //   7 f 1 f 3 f 2 f 4 f 7 f 1 f 3 f 2 f 4 f 7 f 1 f 7 f 4 f 8 f 1 f 3 f 1 f 3 f 2 f 2 f 2 f 4 f 7 f 1 f
  //   3 f 2 f 4 f 8 f 8 f 8 f 8 f 8 f 8 f 8 f 8 f 8 f 8 f 8 f 3 f 1 f 1 f 1 f 8 f 2 f 2 f 2 f 8 f
  //   Keyboard
endmodule
